# Fritzing sketch Sketch (saved by Fritzing 0.9.3b)

parts:
  Raspberry_Pi_1 = Raspberry Pi 3 [part_number=RPI-3-V1.2]
  M1 = BTS7960
  M2 = BTS7960
  PWM1 = PCA9685 16x12-bit PWM Breakout
  GY1 = MPU-6050 Board GY-521 [form="♀ (female)" package=THT]
  Bauteil1 = INA 260

nets:
  N1: Raspberry_Pi_1.3v3, PWM1.no_name_yet#505, PWM1.no_name_yet#605, GY1.pin1
  N2: Raspberry_Pi_1.GPIO2, PWM1.no_name_yet#504, PWM1.no_name_yet#604, GY1.pin4
  N3: Raspberry_Pi_1.GPIO3, PWM1.no_name_yet#503, PWM1.no_name_yet#603, GY1.pin3
  N4: Raspberry_Pi_1.GIPO22, M1.pin3
  N5: Raspberry_Pi_1.GIPO13, M2.pin3
  N6: Raspberry_Pi_1.GIPO19, M2.pin4
  GND: Raspberry_Pi_1.GND, M1.pin8, M2.pin8, PWM1.no_name_yet#501, PWM1.no_name_yet#601, PWM1.no_name_yet#1000, PWM1.no_name_yet#1002, PWM1.no_name_yet#1015, GY1.pin2, Bauteil1.GND
  N7: Raspberry_Pi_1.GIPO23, M1.pin4
  N8: M1.pin1, PWM1.no_name_yet#0
  N9: M1.pin2, PWM1.no_name_yet#1
  N10: M1.pin7, M2.pin7, PWM1.no_name_yet#100, PWM1.no_name_yet#102, PWM1.no_name_yet#115, Bauteil1.VCC
  N11: M2.pin1, PWM1.no_name_yet#2
  N12: M2.pin2, PWM1.no_name_yet#3

custom parts:
  BTS7960: BTS7960 43A Peak Power H-Bridge PWM Motor Driver
  MPU-6050 Board GY-521: Acelerometro y Giroscopio MPU-6050 Board GY-521
  INA 260: Rev. B, add copy
